# Fritzing sketch Circuit_Diagram (saved by Fritzing 1.0.2b)

parts:
  Mod2 = Raspberry Pi Pico
  L298N1 = L298N DC motor driver
  M1 = DC Motor [voltage_(max)=6V voltage_(min)=3V]
  M2 = DC Motor [voltage_(max)=6V voltage_(min)=3V]
  M3 = DC Motor [voltage_(max)=6V voltage_(min)=3V]
  M4 = DC Motor [voltage_(max)=6V voltage_(min)=3V]
  D2F1 = D2F-FL Omron Snap Action Limit Switch with Level
  D2F2 = D2F-FL Omron Snap Action Limit Switch with Level
  D2F3 = D2F-FL Omron Snap Action Limit Switch with Level
  D2F4 = D2F-FL Omron Snap Action Limit Switch with Level
  M5 = RioRand LM2596
  U1 = TCRT5000 [package=THT]
  U2 = TCRT5000 [package=THT]
  U3 = TCRT5000 [package=THT]
  U4 = TCRT5000 [package=THT]
  U5 = TCRT5000 [package=THT]
  U6 = TCRT5000 [package=THT]
  U7 = TCRT5000 [package=THT]
  U8 = TCRT5000 [package=THT]
  R7 = Resistor [tolerance=±5% resistance=120 package="1206 [SMD]"]
  LED1 = LED - 5mm [color="White (4500K)" current=0.030A package="5 mm [THT]"]
  LED2 = LED - 5mm [color="White (4500K)" current=0.030A package="5 mm [THT]"]
  LED3 = LED - 5mm [color="White (4500K)" current=0.030A package="5 mm [THT]"]
  LED4 = LED - 5mm [color="White (4500K)" current=0.030A package="5 mm [THT]"]
  R8 = Resistor [tolerance=±5% resistance=120 package="1206 [SMD]"]
  R9 = Resistor [tolerance=±5% resistance=120 package="1206 [SMD]"]
  R10 = Resistor [tolerance=±5% resistance=120 package="1206 [SMD]"]
  R11 = Resistor [tolerance=±5% resistance=120 package="1206 [SMD]"]
  R12 = Resistor [tolerance=±5% resistance=120 package="1206 [SMD]"]
  R13 = Resistor [tolerance=±5% resistance=120 package="1206 [SMD]"]
  R14 = Resistor [tolerance=±5% resistance=10k package="1206 [SMD]"]
  R15 = Resistor [tolerance=±5% resistance=10k package="1206 [SMD]"]
  R16 = Resistor [tolerance=±5% resistance=10k package="1206 [SMD]"]
  R17 = Resistor [tolerance=±5% resistance=10k package="1206 [SMD]"]
  R18 = Resistor [tolerance=±5% resistance=10k package="1206 [SMD]"]
  R19 = Resistor [tolerance=±5% resistance=10k package="1206 [SMD]"]
  R20 = Resistor [tolerance=±5% resistance=10k package="1206 [SMD]"]
  R21 = Resistor [tolerance=±5% resistance=10k package="1206 [SMD]"]
  R22 = Resistor [tolerance=±5% resistance=120 package="1206 [SMD]"]
  Mod1 = Raspberry Pi Pico
  M7 = RioRand LM2596
  S1 = Toggle Switch [package=THT]
  S2 = Toggle Switch [package=THT]
  S3 = Toggle Switch [package=THT]
  R25 = Resistor [tolerance=±5% resistance=180 package="1206 [SMD]"]
  R26 = Resistor [tolerance=±5% resistance=180 package="1206 [SMD]"]
  R27 = Resistor [tolerance=±5% resistance=180 package="1206 [SMD]"]
  R28 = Resistor [tolerance=±5% resistance=180 package="1206 [SMD]"]
  Part9 = Jtron 1 Channel Optoisolated Relay Module [package=relay]
  Power_plug2 = Power plug
  CUI-enc4 = AMT103
  CUI-enc5 = AMT103
  CUI-enc6 = AMT103
  CUI-enc7 = AMT103
  LED5 = LED - 5mm [color="Green (555nm)" current=0.030A package="5 mm [THT]"]
  R29 = Resistor [tolerance=±5% resistance=120 package="1206 [SMD]"]
  Part10 = InvenSense MPU6050
  Q1 = Basic FET N-Channel [package="D2Pak [SMD]"]
  HCF_1 = HCF 4067 [package="DIP24 [THT]"]
  Part11 = HY-SRF05 Ultrasonic Rangefinder
  Part12 = HY-SRF05 Ultrasonic Rangefinder
  Part13 = HY-SRF05 Ultrasonic Rangefinder
  Part14 = HY-SRF05 Ultrasonic Rangefinder
  Part16 = Logic Level Converter [part_number=Bi-directional]
  Part17 = Logic Level Converter
  R30 = Resistor [tolerance=±5% resistance=220 package="1206 [SMD]"]
  Part18 = HY-SRF05 Ultrasonic Rangefinder
  R31 = Resistor [tolerance=±5% resistance=10k package="1206 [SMD]"]
  R37 = Resistor [tolerance=±5% resistance=4.7k package="1206 [SMD]"]  # not connected
  R38 = Resistor [tolerance=±5% resistance=4.7k package="1206 [SMD]"]  # not connected
  R39 = Resistor [tolerance=±5% resistance=4.7k package="1206 [SMD]"]  # not connected
  R40 = Resistor [tolerance=±5% resistance=4.7k package="1206 [SMD]"]  # not connected
  R41 = Resistor [tolerance=±5% resistance=4.7k package="1206 [SMD]"]  # not connected
  R42 = Resistor [tolerance=±5% resistance=4.7k package="1206 [SMD]"]  # not connected
  R43 = Resistor [tolerance=±5% resistance=4.7k package="1206 [SMD]"]  # not connected
  R44 = Resistor [tolerance=±5% resistance=4.7k package="1206 [SMD]"]
  C1 = Capacitor [package=cap-pth-small2]
  F1 = FUSE [part_number="5A Fuse" package=fuse_5mm]
  D1 = Schottky Diode [part_number=1N5822 package="300 mil [THT]"]
  Power_plug3 = Power plug
  R45 = Resistor [tolerance=±5% resistance=10k package="1206 [SMD]"]
  R46 = Resistor [tolerance=±5% resistance=2.7k package="1206 [SMD]"]
  R47 = Resistor [tolerance=±5% resistance=120 power=0.25W package=THT]
  R48 = Resistor [tolerance=±5% resistance=120 power=0.25W package=THT]
  R49 = Resistor [tolerance=±5% resistance=120 power=0.25W package=THT]
  R50 = Resistor [tolerance=±5% resistance=120 power=0.25W package=THT]
  Mod3 = KY-015 Temperature & Humidity Sensor Module [package="Breakout board"]

nets:
  GND: Mod2.pin_3, Mod2.pin_28, Mod2.pin_38, Mod2.pin_42, D2F1.COM, D2F2.COM, D2F3.COM, D2F4.COM, M5.Pin_4, U5.Pin_2, LED1.cathode, LED2.cathode, LED3.cathode, LED4.cathode, Mod1.pin_3, Mod1.pin_28, Mod1.pin_38, S2.COM, S3.L1, S3.COM, CUI-enc4.GND, CUI-enc5.GND, CUI-enc6.GND, CUI-enc7.GND, LED5.cathode, Part10.GND, HCF_1.12_VSS, HCF_1.15_Inhibit, Part16.GND, Part17.GND, Part18.GND, R31.Pin_1, C1.2
  N1: Mod2.pin_4, Mod1.pin_34
  N2: Mod2.pin_14, D2F4.NO
  N3: Mod2.pin_15, D2F3.NO
  N4: Mod2.pin_16, D2F2.NO
  N5: Mod2.pin_17, D2F1.NO
  N6: Mod2.pin_19, Mod3.S
  N7: Mod2.pin_21, S2.L2
  N8: Mod2.pin_22, S2.L1
  N9: Mod2.pin_24, R28.Pin_1
  N10: Mod2.pin_25, R27.Pin_1
  N11: Mod2.pin_26, R25.Pin_1
  N12: Mod2.pin_27, R26.Pin_1
  N13: Mod2.pin_34, R45.Pin_0
  VCC: Mod2.pin_39, M5.Pin_3, R7.Pin_0, R8.Pin_0, R9.Pin_0, R10.Pin_0, R11.Pin_0, R12.Pin_0, R14.Pin_0, R15.Pin_0, R16.Pin_0, R17.Pin_0, R18.Pin_0, R19.Pin_0, R20.Pin_0, R21.Pin_0, R22.Pin_0, Mod1.pin_39, Part10.VCC, HCF_1.24_Vdd, Part16.LV, Part17.LV, Part18.Vcc, R44.Pin_1, C1.1
  N14: L298N1.OUT1, M3.pin_2, M4.pin_2
  N15: L298N1.OUT2, M3.pin_1, M4.pin_1
  N16: L298N1.OUT3, M1.pin_2, M2.pin_2
  N17: L298N1.OUT4, M1.pin_1, M2.pin_1
  N18: L298N1.12V, M5.Pin_1, M7.Pin_1, D1.cathode, R45.Pin_1
  GND_2: L298N1.GND, M5.Pin_2, M7.Pin_4, Part9.GND, R46.Pin_1
  VCC_2: L298N1.5V#7, M7.Pin_3, Part9.VCC, Part11.Vcc, Part12.Vcc, Part13.Vcc, Part14.Vcc, Part16.HV, Part17.HV, Mod3.Vin
  N19: L298N1.5V#9, L298N1.ENA
  N20: L298N1.5V#10, L298N1.ENB
  N21: L298N1.IN1, Mod1.pin_27
  N22: L298N1.IN2, Mod1.pin_26
  N23: L298N1.IN3, Mod1.pin_25
  N24: L298N1.IN4, Mod1.pin_24
  N25: U1.Pin_1, R16.Pin_1, HCF_1.18_TG13
  N26: U1.Pin_3, U2.Pin_3, U3.Pin_3, U4.Pin_3, U5.Pin_3, U6.Pin_3, U7.Pin_3, U8.Pin_3, Q1.drain
  N27: U1.Pin_4, R10.Pin_1
  N28: U2.Pin_1, R17.Pin_1, HCF_1.19_TG12
  N29: U2.Pin_4, R22.Pin_1
  N30: U3.Pin_1, R14.Pin_1, HCF_1.17_TG14
  N31: U3.Pin_4, R9.Pin_1
  N32: U4.Pin_1, R18.Pin_1, HCF_1.20_TG11
  N33: U4.Pin_4, R11.Pin_1
  N34: U5.Pin_1, R15.Pin_1, HCF_1.16_TG15
  N35: U5.Pin_4, R8.Pin_1
  N36: U6.Pin_1, R19.Pin_1, HCF_1.21_TG10
  N37: U6.Pin_4, R12.Pin_1
  N38: U7.Pin_1, R20.Pin_1, HCF_1.22_TG9
  N39: U7.Pin_4, R7.Pin_1
  N40: U8.Pin_1, R21.Pin_1, HCF_1.23_TG8
  GND_3: U8.Pin_2, Q1.source, Part11.GND, Part12.GND, Part13.GND, Part14.GND, Mod3.-
  N41: U8.Pin_4, R13.Pin_1
  N42: LED1.anode, R28.Pin_0
  N43: LED2.anode, R27.Pin_0
  N44: LED3.anode, R25.Pin_0
  N45: LED4.anode, R26.Pin_0
  N46: Mod1.pin_1, R30.Pin_0, R31.Pin_0
  N47: Mod1.pin_2, R29.Pin_1
  N48: Mod1.pin_4, HCF_1.11_B
  N49: Mod1.pin_5, HCF_1.10_A
  N50: Mod1.pin_6, HCF_1.14_C
  N51: Mod1.pin_7, HCF_1.13_D
  N52: Mod1.pin_9, Part9.IN1
  N53: Mod1.pin_10, CUI-enc4.B
  N54: Mod1.pin_11, CUI-enc7.B
  N55: Mod1.pin_12, CUI-enc4.A
  N56: Mod1.pin_14, CUI-enc7.A
  N57: Mod1.pin_15, CUI-enc6.A
  N58: Mod1.pin_16, CUI-enc5.A
  N59: Mod1.pin_17, Part18.Trig
  N60: Mod1.pin_19, Part10.SDA
  N61: Mod1.pin_20, Part10.SCL
  N62: Mod1.pin_29, CUI-enc6.B
  N63: Mod1.pin_31, HCF_1.1_O/I
  N64: Mod1.pin_32, CUI-enc5.B
  GND_4: M7.Pin_2, Power_plug2.GND, Power_plug3.GND
  N65: S1.L1, Power_plug3.VCC
  N66: S1.COM, Power_plug2.VCC
  N67: S1.L2, F1.1
  N68: CUI-enc4.5V, R47.Pin_1
  N69: CUI-enc5.5V, R48.Pin_1
  N70: CUI-enc6.5V, R49.Pin_1
  N71: CUI-enc7.5V, R50.Pin_1
  N72: LED5.anode, R29.Pin_0
  N73: Q1.Gate, R30.Pin_1
  N74: HCF_1.2_TG_7, Part17.TX2_LV
  N75: HCF_1.3_TG6, Part17.RX2_LV
  N76: HCF_1.4_TG5, Part17.RX_LV
  N77: HCF_1.5_TG4, Part17.TX_LV
  N78: HCF_1.6_TG3, Part16.TX2_LV
  N79: HCF_1.7_TG2, Part16.RX2_LV
  N80: HCF_1.8_TG1, Part16.RX_LV
  N81: HCF_1.9_TG0, Part16.TX_LV
  N82: Part11.Trig, Part17.RX2_HV
  N83: Part11.Echo, Part17.TX2_HV
  N84: Part12.Trig, Part17.TX_HV
  N85: Part12.Echo, Part17.RX_HV
  N86: Part13.Trig, Part16.TX_HV
  N87: Part13.Echo, Part16.RX_HV
  N88: Part14.Trig, Part16.RX2_HV
  N89: Part14.Echo, Part16.TX2_HV
  N90: F1.2, D1.anode
  N91: R47.Pin_0, R48.Pin_0, R49.Pin_0, R50.Pin_0

notes:
  To 3 cell Li-Po battery
  3.3v regulator
  5v regulator
  4 Namiki motors with encoders.
  (I'm not using the AMT103 encoders. Namiki motors come with an encoder however, I could not find a Namiki motor part for Fritzing)
  Edge sensors
  (These will prevent the robot from falling off of an edge)
  Camera LEDs
  IRF540N N-Channel Power MOSFET
  NOTE: This ultrasonic is a SRF05 not a HY-SRF05
  NOT USED.
  Battery charge connector
  NOT USED FOR NOW

custom parts:
  Raspberry Pi Pico: Raspberry Pi Pico. Based around the RP2040 microcontroller the Pico is a low cost microcontroller device bringing Raspberry Pi quality, cost, and easy of use to the microcontroller space. Jan 2021, Split part in to two versions: tht (this one) and SMD. This one will drill holes for a .1 in header in pcb to allow plugging in the module as well as providing pads to solder the module to the top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
  L298N DC motor driver: 2x DC motor driver with 78M05 positive voltage regulator (7..35 V) L298N: max 46 V, 2 A Set 5 V Enable jumper to enable 5 V regultor (needed for the L298N) and +5 V output at screw terminal or supply external +5 V at screw terminal Set ENA and/or ENB to +5 V to enable motor permanently or supply ENA and/or ENB with PWM signal IN1 and IN2 set rotation directory for motor A (OUT1/OUT2) IN2 and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
  D2F-FL Omron Snap Action Limit Switch with Level: Snap action switch with stainless steel lever.
  TCRT5000: TCRT5000 optical reflective sensor
  KY-015 Temperature & Humidity Sensor Module: KY-015 temperature and humidity sensor module, provides a low-latency serial interface to measure humidity and temperature.
